# Fritzing sketch Sketch (saved by Fritzing 0.9.2b)

parts:
  Raspberry_Pi1 = Raspberry Pi 2
  Power_plug1 = Power plug
  パーツ1 = ws2812b [package=THT]
  パーツ2 = ws2812b [package=THT]
  パーツ3 = ws2812b [package=THT]

nets:
  VDD: Raspberry_Pi1.3v3, Raspberry_Pi1.3V3, パーツ1.VDD, パーツ2.VDD, パーツ3.VDD
  VSS: Raspberry_Pi1.GND, Power_plug1.GND, パーツ1.VSS, パーツ2.VSS, パーツ3.VSS
  N1: Raspberry_Pi1.GIPO18, パーツ1.DIN
  5V: Raspberry_Pi1.5V, Power_plug1.VCC
  N2: パーツ1.DOUT, パーツ2.DIN
  N3: パーツ2.DOUT, パーツ3.DIN

notes:
  WS2812Bを26個
  数珠つなぎに接続する
